// Logisim project 8-Bit ALU and Flag Register with Logic Status Unit.circ as structural Verilog: 1 circuit, main circuit main
module main (
  input  [7:0] A,
  input  [7:0] B,
  input  [1:0] Selector,
  input  in_4,
  input  in_5,
  output [7:0] Result
);

  wire clock_1_out, not_1_out, not_2_out, xnor_1_out, xor_1_out, xor_2_out, xor_3_out, xor_4_out, xor_5_out,
       xor_6_out;
  wire [3:0] and_3_out, register_1_q;
  wire [7:0] adder_1_out, and_1_out, or_1_out, subtractor_1_out;

  Adder adder_1 (.a(A), .b(B), .out(adder_1_out), .cout(and_3_out[2]));  // open: cin
  Subtractor subtractor_1 (.a(A), .b(B), .out(subtractor_1_out));  // open: bin, bout
  assign and_1_out = A & B;  // AND_Gate and_1, 8 bits wide
  assign or_1_out = A | B;  // OR_Gate or_1, 8 bits wide
  not not_1 (not_1_out, Selector[1]);
  Multiplexer #(.select(2), .width(8)) multiplexer_1 (
    .in0(adder_1_out), .in1(subtractor_1_out), .in2(and_1_out), .in3(or_1_out), .out(Result), .sel(Selector));
  xor xor_1 (xor_1_out, Result[0], Result[1]);
  xor xor_2 (xor_2_out, Result[2], Result[3]);
  xor xor_3 (xor_3_out, Result[4], Result[5]);
  xor xor_4 (xor_4_out, Result[6], Result[7]);
  xor xor_5 (xor_5_out, xor_1_out, xor_2_out);
  xor xor_6 (xor_6_out, xor_3_out, xor_4_out);
  nor nor_1 (and_3_out[3], Result[0], Result[1], Result[2], Result[3], Result[4], Result[5], Result[6], Result[7]);
  and and_2 (and_3_out[1], Result[7], Selector[0], not_1_out);
  not not_2 (not_2_out, and_3_out[3]);
  and and_3 (and_3_out[0], not_2_out, xnor_1_out);
  xnor xnor_1 (xnor_1_out, xor_5_out, xor_6_out);
  Register #(.width(4)) register_1 (.D(and_3_out), .en(in_4), .clk(clock_1_out), .Q(register_1_q), .clr(in_5));
  Clock clock_1 (.out(clock_1_out));
  LED Zero_Flag (.in(register_1_q[3]));
  LED Carry_Flag (.in(register_1_q[2]));
  LED Negative_Flag (.in(register_1_q[1]));
  LED Parity_flag (.in(register_1_q[0]));

  // Notes on the sheet:
  //   00 = ADD
  //   01 = SUB
  //   10 = AND
  //   11 = OR
  //   8-Bit ALU and Flag Register with Logic Status Unit
endmodule
